// Logisim project playground.circ as structural Verilog: 1 circuit, main circuit main
module main (
  input  in_1,
  input  in_2,
  input  in_3,
  input  in_4,
  input  in_5,
  input  in_6,
  input  in_7,
  input  in_8,
  input  in_9,
  input  in_10
);

  wire and_1_out, and_2_out, and_3_out, and_4_out, and_5_out, and_6_out, and_7_out, and_8_out, and_9_out,
       and_10_out, and_11_out, button_1_out, button_2_out, button_3_out, main_11_o0, main_11_o1, main_11_o2,
       main_11_o3, main_11_o4, main_11_o5, main_11_o6, main_11_o7, main_11_o8, main_11_o9, not_1_out,
       or_1_out;

  // ring_counter_main main_1: pin names not known
  // ring_counter_main main_2: pin names not known
  // ring_counter_main main_3: pin names not known
  // ring_counter_main main_4: pin names not known
  // ring_counter_main main_5: pin names not known
  // ring_counter_main main_6: pin names not known
  Button button_1 (.out(button_1_out));
  Button button_2 (.out(button_2_out));
  // ring_counter_main main_7: pin names not known
  // ring_counter_main main_8: pin names not known
  not not_1 (not_1_out, or_1_out);
  // ring_counter_main main_9: pin names not known
  // ring_counter_main main_10: pin names not known
  ring_counter_main main_11 (
    .Count(and_1_out), .Reset(button_2_out), .o9(main_11_o9), .o8(main_11_o8), .o7(main_11_o7),
    .o6(main_11_o6), .o5(main_11_o5), .o4(main_11_o4), .o3(main_11_o3), .o2(main_11_o2), .o1(main_11_o1),
    .o0(main_11_o0));
  and and_1 (and_1_out, button_1_out, not_1_out);
  // ring_counter_main main_12: pin names not known
  // ring_counter_main main_13: pin names not known
  // ring_counter_main main_14: pin names not known
  // ring_counter_main main_15: pin names not known
  // ring_counter_main main_16: pin names not known
  // ring_counter_main main_17: pin names not known
  and and_2 (and_2_out, main_11_o9, in_1);
  and and_3 (and_3_out, main_11_o8, in_2);
  and and_4 (and_4_out, main_11_o7, in_3);
  and and_5 (and_5_out, main_11_o6, in_4);
  and and_6 (and_6_out, main_11_o5, in_5);
  and and_7 (and_7_out, main_11_o4, in_6);
  and and_8 (and_8_out, main_11_o3, in_7);
  and and_9 (and_9_out, main_11_o2, in_8);
  and and_10 (and_10_out, main_11_o1, in_9);
  and and_11 (and_11_out, main_11_o0, in_10);
  // ring_counter_main main_18: pin names not known
  // ring_counter_main main_19: pin names not known
  Button button_3 (.out(button_3_out));
  or or_1 (or_1_out, and_2_out, and_3_out, and_4_out, and_5_out, and_6_out, and_7_out, and_8_out, and_9_out, and_10_out, and_11_out);
  // ring_counter_main main_20: pin names not known
  ring_counter_main main_21 (.Count(and_1_out), .Reset(button_3_out));  // open: o9, o8, o7, o6, o5, o4, o3, o2, o1, o0
endmodule
