// Logisim project ring_counter.circ as structural Verilog: 1 circuit, main circuit main
module main (
  input  Count,
  input  Reset,
  output o9,
  output o8,
  output o7,
  output o6,
  output o5,
  output o4,
  output o3,
  output o2,
  output o1,
  output o0
);

  D_Flip_Flop d_ff_1 (.clk(Count), .D(o8), .Q(o9), .reset(Reset));  // open: Qn, preset, en
  D_Flip_Flop d_ff_2 (.clk(Count), .D(o7), .Q(o8), .reset(Reset));  // open: Qn, preset, en
  D_Flip_Flop d_ff_3 (.clk(Count), .D(o6), .Q(o7), .reset(Reset));  // open: Qn, preset, en
  D_Flip_Flop d_ff_4 (.clk(Count), .D(o5), .Q(o6), .reset(Reset));  // open: Qn, preset, en
  D_Flip_Flop d_ff_5 (.clk(Count), .D(o4), .Q(o5), .reset(Reset));  // open: Qn, preset, en
  D_Flip_Flop d_ff_6 (.clk(Count), .D(o3), .Q(o4), .reset(Reset));  // open: Qn, preset, en
  D_Flip_Flop d_ff_7 (.clk(Count), .D(o2), .Q(o3), .reset(Reset));  // open: Qn, preset, en
  D_Flip_Flop d_ff_8 (.clk(Count), .D(o1), .Q(o2), .reset(Reset));  // open: Qn, preset, en
  D_Flip_Flop d_ff_9 (.clk(Count), .D(o0), .Q(o1), .reset(Reset));  // open: Qn, preset, en
  D_Flip_Flop d_ff_10 (.clk(Count), .D(o9), .Q(o0), .preset(Reset));  // open: Qn, en, reset
endmodule
